# Fritzing sketch Pamoka1_1 (saved by Fritzing 0.9.10b)
breadboards: 1

parts:
  VCC1 = Battery
  L1 = Solenoid
  S1 = Pushbutton [package="[THT]"]

nets:
  N1: VCC1.-, L1.pin1
  N2: VCC1.+, S1.Pin_3, S1.Pin_4
  N3: L1.pin2, S1.Pin_1, S1.Pin_2
