# Fritzing sketch Pamoka1_2 (saved by Fritzing 0.9.10b)
breadboards: 1

parts:
  VCC1 = Battery
  L1 = Solenoid
  S1 = Pushbutton [package="[THT]"]
  VM2 = Multimeter (DC Voltage)

nets:
  N1: VCC1.-, L1.pin1, VM2.COM_Probe
  N2: VCC1.+, S1.Pin_3, S1.Pin_4, VM2.A_Probe
  N3: L1.pin2, S1.Pin_1, S1.Pin_2
